# Fritzing sketch lighttable (saved by Fritzing 0.9.1b)
breadboards: 1

parts:
  Teensy_3_1 = Teensy 3.1
  R2 = Photocell (LDR) [package=THT]
  part = Electrolytic Capacitor [capacitance=100µF package="100 mil [THT, electrolytic]"]
  part_2 = Resistor [tolerance=±5% resistance=10k package=THT]

nets:
  N1: Teensy_3_1.A14/DAC, part.+
  N2: R2.pin_0, part_2.Pin_0

notes:
  parts:
  10k Ohm resistor
  Photoresistor/LDR
  100µF elko
  Teensy 3.1
  greens wire is the audio output and connects to a mixer/headphones
  audio output
